# Fritzing sketch PS4Controlled_ArmBot_ESP32 (saved by Fritzing 0.9.4)
circuit board: 8.46667cm x 5.64444cm
breadboards: 1

parts:
  U1 = ESP32-38PinWide [part_number=ESP32-38PinWide]
  J1 = Basic Servo
  J2 = Basic Servo
  J3 = Basic Servo
  L298N1 = L298N DC motor driver
  M1 = DC Motor
  M2 = DC Motor
  J4 = Basic Servo
  Power_plug1 = Power plug
  LED1 = smd LED [color="Green (555nm)" package="0805 [SMD]"]
  LED2 = smd LED [color="Red (633nm)" package="0805 [SMD]"]
  LED11 = smd LED [color="Red (633nm)" package="0805 [SMD]"]
  LED12 = smd LED [color="Red (633nm)" package="0805 [SMD]"]
  LED13 = smd LED [color="Orange (620nm)" package="0805 [SMD]"]
  LED14 = smd LED [color="Orange (620nm)" package="0805 [SMD]"]
  LED15 = smd LED [color="Orange (620nm)" package="0805 [SMD]"]
  LED16 = smd LED [color="Orange (620nm)" package="0805 [SMD]"]

nets:
  N1: U1.GPIO33, J4.pulse
  N2: U1.GPIO25, J3.pulse
  N3: U1.GPIO26, J2.pulse
  N4: U1.GPIO27, J1.pulse
  N5: U1.GND, LED2.cathode, LED11.cathode, LED12.cathode, LED13.cathode, LED14.cathode, LED15.cathode, LED16.cathode
  N6: U1.GPIO16, LED2.anode
  N7: U1.GPIO17, L298N1.IN1
  N8: U1.GPIO5, L298N1.IN2
  N9: U1.GPIO18, L298N1.IN3
  N10: U1.GPIO19, L298N1.IN4
  N11: U1.GPIO21, LED1.anode
  N12: U1.GPIO22, L298N1.ENB
  N13: U1.GPIO23, L298N1.ENA
  GND: J1.gnd, J2.gnd, J3.gnd, J4.gnd
  VCC: J1.vcc, J2.vcc, J3.vcc, L298N1.5V, J4.vcc
  N14: L298N1.OUT1, M2.pin_2
  N15: L298N1.OUT2, M2.pin_1
  N16: L298N1.OUT3, M1.pin_2
  N17: L298N1.OUT4, M1.pin_1
  12V: L298N1.12V, Power_plug1.VCC
  GND_2: L298N1.GND, Power_plug1.GND

custom parts:
  ESP32-38PinWide: Generic 38-Pin ESP32 with wide format (only access to one side of pins on a breadboard) based on Stephen Lilley's HiLetgo ESP-WROOM-32 ESP32 ESP-32S Development Board.
  L298N DC motor driver: 2x DC motor driver with 78M05 positive voltage regulator (7..35 V) L298N: max 46 V, 2 A Set 5 V Enable jumper to enable 5 V regultor (needed for the L298N) and +5 V output at screw terminal or supply external +5 V at screw terminal Set ENA and/or ENB to +5 V to enable motor permanently or supply ENA and/or ENB with PWM signal IN1 and IN2 set rotation directory for motor A (OUT1/OUT2) IN2 and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
